# Fritzing sketch oximeter (saved by Fritzing 0.9.1b)
perfboards: 1

parts:
  part = Resistor [tolerance=±5% resistance=15k package=THT]
  OLED_Display = Grove OLED 128x96
  part_2 = Resistor [tolerance=±5% resistance=15k package=THT]
  part_3 = LED - 5mm [color="Infrared (940nm)" package="5 mm [THT]"]
  U3 = OP37 - Low Noise, Precision, High Speed Op Amp [part_number=OP37]
  part_4 = Resistor [tolerance=±5% resistance=220 package=THT]
  Part1 = Arduino Nano (Rev3.0)
  part_5 = LED - 5mm [color="Red (660nm)" package="5 mm [THT]"]
  part_6 = Resistor [tolerance=±5% resistance=470 package=THT]
  PhotoDiode = S1133 Si Photodiode [package="8mm Ceramic [THT]"]

nets:
  N1: part.Pin_0, part_2.Pin_1
  N2: part.Pin_1, U3.OUT, Part1.A7
  GND: OLED_Display.GND, part_3.cathode, U3.-V, part_4.Pin_1, Part1.GND, part_5.cathode
  VCC: OLED_Display.VCC, Part1.3V3
  N3: OLED_Display.SDA, Part1.A4
  N4: OLED_Display.SCL, Part1.A5
  N5: part_2.Pin_0, U3.-IN, PhotoDiode.cathode
  N6: part_3.anode, Part1.D3
  N7: U3.+IN, part_4.Pin_0
  N8: U3.V+, part_6.Pin_0
  N9: Part1.D5, part_5.anode
  N10: Part1.5V, part_6.Pin_1

notes:
  Op Amp shown is OP37
  Currently using CA3140AEZ
